# Fritzing sketch LedPcb (saved by Fritzing 0.9.3b)
circuit board: 8.13165cm x 6.48082cm
breadboards: 1

parts:
  J8 = shrouded pin header, 10 pins [form="♂ (shrouded male)"]
  J6 = female pin header, 3 pins [form="♀ (female)"]
  J9 = shrouded pin header, 10 pins [form="♂ (shrouded male)"]
  J7 = female pin header, 3 pins [form="♀ (female)"]

nets:
  N1: J8.pin3, J6.pin1, J9.pin3
  N2: J8.pin4, J6.pin2, J9.pin2
  N3: J8.pin5, J6.pin3, J9.pin1
  N4: J8.pin7, J9.pin9
  N5: J8.pin8, J9.pin8, J7.pin3
  N6: J8.pin9, J7.pin1
  N7: J8.pin10, J9.pin6, J7.pin2

notes:
  G
  R
  +
  -
  B
